# Fritzing sketch Mapper85_DonkeyKongCountry4VRC7 (saved by Fritzing 1.0.3b)
circuit board: 9.00001cm x 5.68cm
breadboards: 1

parts:
  1-30 = Generic single row SMD female header - 30 pins [form="♀ (female)" package=THT]
  60-31 = Generic single row SMD female header - 30 pins [form="♀ (female)" package=THT]
  3_58MHz = Crystal [frequency="16 Mhz" package=SMD]
  VRC7 = IC, DIP package, 48 pins [chip_label=IC]
  LM358 = LM 358 Dual Op-Amp [package="DIP8 [THT]"]
  LM359 = LM 358 Dual Op-Amp [package="SO 08 [SMD]"]
  27K = Resistor [tolerance=±5% power=0.25W resistance=220 package=THT]
  IC2 = IC, DIP package, 32 pins [chip_label=IC]
  2_2K = Resistor [tolerance=±5% power=0.25W resistance=220 package=THT]
  4_7nF = Ceramic Capacitor [capacitance=100nF voltage=35V package="100 mil [THT, multilayer]"]
  33K = Resistor [tolerance=±5% power=0.25W resistance=220 package=THT]
  1uF = Ceramic Capacitor [capacitance=100nF voltage=35V package="100 mil [THT, multilayer]"]
  22uF = Ceramic Capacitor [capacitance=100nF voltage=35V package="100 mil [THT, multilayer]"]
  4_3K = Resistor [tolerance=±5% power=0.25W resistance=220 package=THT]
  240K = Resistor [tolerance=±5% power=0.25W resistance=220 package=THT]
  910 = Resistor [tolerance=±5% power=0.25W resistance=220 package=THT]
  3_9K = Resistor [tolerance=±5% power=0.25W resistance=220 package=THT]
  2_2K_2 = Resistor [tolerance=±5% power=0.25W resistance=220 package=THT]
  IC3 = IC, DIP package, 32 pins [chip_label=IC]

nets:
  N1: 1-30.pin1, IC3.pin16
  N2: 1-30.pin10, VRC7.pin19
  N3: 1-30.pin16, LM358.connector3, LM359.connector3, 2_2K.Pin_0, 4_7nF.1, 33K.Pin_0, 1uF.0, 22uF.1, 910.Pin_1
  N4: 1-30.pin30, VRC7.pin42, LM358.connector4, LM358.connector5, LM358.connector7, LM359.connector4, LM359.connector5, LM359.connector7, 1uF.1
  N5: 60-31.pin6, VRC7.pin33
  N6: 60-31.pin7, VRC7.pin32
  N7: 60-31.pin8, VRC7.pin31
  N8: 60-31.pin15, 3_9K.Pin_0, 2_2K_2.Pin_1
  N9: 60-31.pin16, 3_9K.Pin_1
  N10: 60-31.pin26, VRC7.pin29
  N11: 60-31.pin27, VRC7.pin28
  N12: 60-31.pin28, VRC7.pin27
  N13: 3_58MHz.pin_0, VRC7.pin18
  N14: 3_58MHz.pin_1, VRC7.pin17
  N15: VRC7.pin20, IC3.pin28
  N16: VRC7.pin21, IC3.pin29
  N17: VRC7.pin22, IC3.pin3
  N18: VRC7.pin23, IC3.pin2
  N19: VRC7.pin25, IC3.pin30
  N20: VRC7.pin26, IC3.pin31
  N21: VRC7.pin34, IC2.pin23
  N22: VRC7.pin35, IC2.pin25
  N23: VRC7.pin36, IC2.pin4
  N24: VRC7.pin37, IC2.pin28
  N25: VRC7.pin38, IC2.pin29
  N26: VRC7.pin39, IC2.pin3
  N27: VRC7.pin40, IC2.pin2
  N28: VRC7.pin41, IC2.pin30
  N29: VRC7.pin43, 27K.Pin_1, 2_2K.Pin_1
  N30: VRC7.pin44, IC3.pin22
  N31: LM358.connector0, LM359.connector0, 240K.Pin_1, 910.Pin_0, 2_2K_2.Pin_0
  N32: LM358.connector1, LM359.connector1, 4_3K.Pin_0, 240K.Pin_0
  N33: LM358.connector2, LM359.connector2, 27K.Pin_0, 4_7nF.0, 33K.Pin_1
  N34: LM358.connector6, LM359.connector6
  N35: 22uF.0, 4_3K.Pin_1

notes:
  4 VRC7 Hack Repro PCB
  Designed by HeeminYT

custom parts:
  Generic single row SMD female header - 30 pins: Generic single row SMD female header
